// Logisim project MIPS8bits.circ as structural Verilog: 2 circuits, main circuit Mini-Mips-8bits
module Mini_Mips_8bits (
  input  IncPc,
  input  Clear,
  input  EscReg,
  input  ClearReg,
  input  RegDst,
  input  UlaFonte,
  input  [2:0] ControleULA,
  input  EscMem,
  input  ClearData,
  input  MemParaReg,
  output [3:0] OPCODE,
  output [7:0] SaidaULA,
  output [7:0] Entrada_B_Reg,
  output [7:0] Op1,
  output out_15,
  output [7:0] Op2,
  output [7:0] \Endereço ,
  output [7:0] Data,
  output [15:0] \Instrução 
);

  wire clk, not_1_out;
  wire [2:0] banco_registradores_mini_mips8bits_smux_1_p3;
  wire [7:0] ram_1_data;

  Clock u_Clk (.out(clk));
  // Busca_Instrução busca_instrução_1: pin names not known; wires that end beside it: IncPc, clk, Clear, \Endereço 
  Hex_Digit_Display hex_digit_display_1 (.value(\Endereço [7:4]), .dp(1'b1));
  Hex_Digit_Display hex_digit_display_2 (.value(\Endereço [3:0]), .dp(1'b1));
  ROM #(.dataWidth(16)) rom_1 (.addr(\Endereço ), .data(\Instrução ));  // open: sel
  // Banco_registradores_Mini_Mips8Bits_sMux banco_registradores_mini_mips8bits_smux_1: pin names not known; wires that end beside it: \Instrução [11:9], \Instrução [8:6], banco_registradores_mini_mips8bits_smux_1_p3, Entrada_B_Reg, EscReg, clk, ClearReg, Op1, Data
  Multiplexer #(.width(3)) multiplexer_1 (
    .in0(\Instrução [8:6]), .in1(\Instrução [5:3]), .out(banco_registradores_mini_mips8bits_smux_1_p3),
    .sel(RegDst));  // open: en
  Multiplexer #(.width(8)) multiplexer_2 (
    .in0(Data), .in1({2'b00, \Instrução [5:0]}), .out(Op2), .sel(UlaFonte));  // open: en
  ULA ula_1 (.Flag(out_15), .resultado(SaidaULA), ._001____SUB(ControleULA), .in_2(Op2), .in_3(Op1));
  not not_1 (not_1_out, EscMem);
  RAM #(.bus("separate")) ram_1 (
    .addr(SaidaULA), .din(Data), .data(ram_1_data), .str(EscMem), .clk(clk), .ld(not_1_out), .clr(ClearData));  // open: sel
  Multiplexer #(.width(8)) multiplexer_3 (
    .in0(ram_1_data), .in1(SaidaULA), .out(Entrada_B_Reg), .sel(MemParaReg));  // open: en

  assign OPCODE = \Instrução [15:12];

  // Notes on the sheet:
  //   OPCODE: pull=down
  //   EscMem: pull=up
  //   Endereço: pull=down
  //   MemParaReg: pull=up
  //   ClearData: pull=down
  //   ControleULA: pull=up
  //   Clear: pull=down
  //   RegDst: pull=up
  //   UlaFonte: pull=up
  //   ClearReg: pull=down
  //   Instrução: pull=down
  //   IncPc: pull=down
  //   EscReg: pull=up
  //   contents of rom_1 (hex, n*v repeats v):
  //   0 2085 2043 458 210a 6080 6104 4044
  //   addi $0 $2 5 	=> $2 = 0+5 
  //   addi S0 S1 3 	=> $1 = 0+3
  //   add  $2 $1 $3	=> $3 = $2+$1
  //   addi $0 $4 10 	=> $4 = 0+10
  //   sw   $0 $2 0	=> M[$0+0]= $2
  //   sw   $0 $4 4	=> M[$0+4]= $4
  //   lw   $0 $1 4	=> $4 = M[$0+4]
endmodule

// RegDst
module Mini_MIPS_8bits_Controle (
  input  ClearReg,
  input  Clear,
  input  ClearData,
  output [3:0] OPCODE,
  output [7:0] SaidaULA,
  output [7:0] Entrada_B_Reg,
  output [7:0] Op1,
  output out_8,
  output [7:0] Op2,
  output [7:0] \Endereço ,
  output [7:0] Data,
  output [15:0] \Instrução ,
  output [2:0] ControleUla,
  output RegDst,
  output EscMem,
  output MemParaReg,
  output UlaFonte
);

  wire clk, EscReg, IncPc, not_1_out;
  wire [2:0] banco_registradores_mini_mips8bits_smux_1_p3;
  wire [7:0] ram_1_data;

  Clock u_Clk (.out(clk));
  // Busca_Instrução busca_instrução_1: pin names not known; wires that end beside it: IncPc, clk, Clear, \Endereço 
  Hex_Digit_Display hex_digit_display_1 (.value(\Endereço [7:4]), .dp(1'b1));
  Hex_Digit_Display hex_digit_display_2 (.value(\Endereço [3:0]), .dp(1'b1));
  ControleMiniMips controleminimips_1 (
    .OP3(\Instrução [15]), .IncPC(IncPc), .OP2(\Instrução [14]), .OP1(\Instrução [13]), .RegDst(RegDst),
    .OP0(\Instrução [12]), .UlaFonte(UlaFonte), .MemParaReg(MemParaReg), .EscReg(EscReg), .EscMem(EscMem),
    .ControleUla2(ControleUla[2]), .ControleUla1(ControleUla[1]), .ControleUla0(ControleUla[0]));
  ROM #(.dataWidth(16)) rom_1 (.addr(\Endereço ), .data(\Instrução ));  // open: sel
  // Banco_registradores_Mini_Mips8Bits_sMux banco_registradores_mini_mips8bits_smux_1: pin names not known; wires that end beside it: \Instrução [11:9], \Instrução [8:6], banco_registradores_mini_mips8bits_smux_1_p3, Entrada_B_Reg, EscReg, clk, ClearReg, Op1, Data
  Multiplexer #(.width(3)) multiplexer_1 (
    .in0(\Instrução [8:6]), .in1(\Instrução [5:3]), .out(banco_registradores_mini_mips8bits_smux_1_p3),
    .sel(RegDst));  // open: en
  Multiplexer #(.width(8)) multiplexer_2 (
    .in0(Data), .in1({2'b00, \Instrução [5:0]}), .out(Op2), .sel(UlaFonte));  // open: en
  ULA ula_1 (.Flag(out_8), .resultado(SaidaULA), ._001____SUB(ControleUla), .in_2(Op2), .in_3(Op1));
  not not_1 (not_1_out, EscMem);
  RAM #(.bus("separate")) ram_1 (
    .addr(SaidaULA), .din(Data), .data(ram_1_data), .str(EscMem), .clk(clk), .ld(not_1_out), .clr(ClearData));  // open: sel
  Multiplexer #(.width(8)) multiplexer_3 (
    .in0(ram_1_data), .in1(SaidaULA), .out(Entrada_B_Reg), .sel(MemParaReg));  // open: en

  assign OPCODE = \Instrução [15:12];

  // Notes on the sheet:
  //   ClearReg: pull=down
  //   Instrução: pull=down
  //   OPCODE: pull=down
  //   EscMem: pull=down
  //   RegDst: pull=down
  //   UlaFonte: pull=down
  //   ControleUla: pull=down
  //   ClearData: pull=down
  //   MemParaReg: pull=down
  //   Clear: pull=down
  //   Endereço: pull=down
  //   contents of rom_1 (hex, n*v repeats v):
  //   0 2085 2043 458 210a 6080 6104 4044
  //   addi $0 $2 5 	=> $2 = 0+5 
  //   addi S0 S1 3 	=> $1 = 0+3
  //   add  $2 $1 $3	=> $3 = $2+$1
  //   addi $0 $4 10 	=> $4 = 0+10
  //   sw   $0 $2 0	=> M[$0+0]= $2
  //   sw   $0 $4 4	=> M[$0+4]= $4
  //   lw   $0 $1 4	=> $4 = M[$0+4]
endmodule
