// Logisim project ULA.circ as structural Verilog
module ULA (
  input  [2:0] _001____SUB,
  input  [7:0] in_2,
  input  [7:0] in_3,
  output Flag,
  output [7:0] resultado
);

  wire [7:0] and_1_resultado, or_1_resultado, somador_subtrator_1_resultado;

  Somador_Subtrator somador_subtrator_1 (
    .in_1(_001____SUB[0]), .Operando_1(in_3), .Operando_2(in_2), .resultado(somador_subtrator_1_resultado),
    .Flag(Flag));
  AND and_1 (.resultado(and_1_resultado), .in_1(in_3), .in_2(in_2));
  OR or_1 (.resultado(or_1_resultado), .in_1(in_3), .in_2(in_2));
  Multiplexer #(.select(3), .width(8)) multiplexer_1 (
    .in0(somador_subtrator_1_resultado), .in1(somador_subtrator_1_resultado),
    .in2(somador_subtrator_1_resultado), .in3(and_1_resultado), .in4(somador_subtrator_1_resultado),
    .in5(or_1_resultado), .in6(somador_subtrator_1_resultado), .in7({8{1'b0}}), .out(resultado),
    .sel(_001____SUB));  // open: en

  // Other names for the same wires on the sheet: operando_1[7:0] = in_2; operando_2[7:0] = in_3;
  //   UlaOp[2:0] = _001____SUB

  // Notes on the sheet:
  //   _001____SUB: pull=down
  //   in_3: pull=down
  //   in_2: pull=down
  //   Flag: pull=down
  //   000 -> ADD 
  //   010 -> ADDi 
  //   011 -> AND 
  //   100 -> LW   
  //   101 -> OR 
  //   110 -> SW 
  //   111 -> zero 
  //   000 -> ADD 
  //   001 -> SUB 
  //   010 -> ADDi 
  //   011 -> AND 
  //   100 -> LW   
  //   101 -> OR 
  //   110 -> SW 
  //   111 -> zero 
endmodule

module Somador_Subtrator (
  input  in_1,
  input  [7:0] Operando_1,
  input  [7:0] Operando_2,
  output [7:0] resultado,
  output Flag
);

  wire adder_1_cout, adder_2_cout, adder_3_cout, adder_4_cout, adder_5_cout, adder_6_cout, adder_7_cout,
       adder_8_cout, xor_1_out, xor_2_out, xor_3_out, xor_4_out, xor_5_out, xor_6_out, xor_7_out, xor_8_out;

  xor xor_1 (xor_1_out, Operando_1[0], in_1);
  xor xor_2 (xor_2_out, Operando_1[1], in_1);
  xor xor_3 (xor_3_out, Operando_1[2], in_1);
  xor xor_4 (xor_4_out, Operando_1[3], in_1);
  xor xor_5 (xor_5_out, Operando_1[4], in_1);
  xor xor_6 (xor_6_out, Operando_1[5], in_1);
  xor xor_7 (xor_7_out, Operando_1[6], in_1);
  xor xor_8 (xor_8_out, Operando_1[7], in_1);
  Adder #(.width(1)) adder_1 (.a(xor_1_out), .b(Operando_2[0]), .out(resultado[0]), .cin(in_1), .cout(adder_1_cout));
  Adder #(.width(1)) adder_2 (
    .a(xor_2_out), .b(Operando_2[1]), .out(resultado[1]), .cin(adder_1_cout), .cout(adder_2_cout));
  Adder #(.width(1)) adder_3 (
    .a(xor_3_out), .b(Operando_2[2]), .out(resultado[2]), .cin(adder_2_cout), .cout(adder_3_cout));
  Adder #(.width(1)) adder_4 (
    .a(xor_4_out), .b(Operando_2[3]), .out(resultado[3]), .cin(adder_3_cout), .cout(adder_4_cout));
  Adder #(.width(1)) adder_5 (
    .a(xor_5_out), .b(Operando_2[4]), .out(resultado[4]), .cin(adder_4_cout), .cout(adder_5_cout));
  Adder #(.width(1)) adder_6 (
    .a(xor_6_out), .b(Operando_2[5]), .out(resultado[5]), .cin(adder_5_cout), .cout(adder_6_cout));
  Adder #(.width(1)) adder_7 (
    .a(xor_7_out), .b(Operando_2[6]), .out(resultado[6]), .cin(adder_6_cout), .cout(adder_7_cout));
  Adder #(.width(1)) adder_8 (
    .a(xor_8_out), .b(Operando_2[7]), .out(resultado[7]), .cin(adder_7_cout), .cout(adder_8_cout));
  xor xor_9 (Flag, adder_8_cout, adder_7_cout);
  LED led_1 (.in(Flag));
  LED led_2 (.in(resultado[6]));
  LED led_3 (.in(resultado[7]));
  LED led_4 (.in(resultado[4]));
  LED led_5 (.in(resultado[5]));
  LED led_6 (.in(resultado[3]));
  LED led_7 (.in(resultado[2]));
  LED led_8 (.in(resultado[1]));
  LED led_9 (.in(resultado[0]));

  // Other names for the same wires on the sheet: op = in_1

  // Notes on the sheet:
  //   Operando_1: pull=down
  //   resultado: pull=down
  //   Operando_2: pull=down
endmodule

module AND (
  input  [7:0] in_1,
  input  [7:0] in_2,
  output [7:0] resultado
);

  and and_1 (resultado[0], in_1[0], in_2[0]);
  and and_2 (resultado[1], in_1[1], in_2[1]);
  and and_3 (resultado[2], in_1[2], in_2[2]);
  and and_4 (resultado[3], in_1[3], in_2[3]);
  and and_5 (resultado[4], in_1[4], in_2[4]);
  and and_6 (resultado[5], in_1[5], in_2[5]);
  and and_7 (resultado[6], in_1[6], in_2[6]);
  and and_8 (resultado[7], in_1[7], in_2[7]);
  LED led_1 (.in(resultado[7]));
  LED led_2 (.in(resultado[6]));
  LED led_3 (.in(resultado[4]));
  LED led_4 (.in(resultado[5]));
  LED led_5 (.in(resultado[1]));
  LED led_6 (.in(resultado[3]));
  LED led_7 (.in(resultado[2]));
  LED led_8 (.in(resultado[0]));

  // Other names for the same wires on the sheet: operando_1[7:0] = in_1; operando_2[7:0] = in_2
endmodule

module OR (
  input  [7:0] in_1,
  input  [7:0] in_2,
  output [7:0] resultado
);

  or or_1 (resultado[0], in_1[0], in_2[0]);
  or or_2 (resultado[1], in_1[1], in_2[1]);
  or or_3 (resultado[2], in_1[2], in_2[2]);
  or or_4 (resultado[3], in_1[3], in_2[3]);
  or or_5 (resultado[4], in_1[4], in_2[4]);
  or or_6 (resultado[5], in_1[5], in_2[5]);
  or or_7 (resultado[6], in_1[6], in_2[6]);
  or or_8 (resultado[7], in_1[7], in_2[7]);
  LED led_1 (.in(resultado[6]));
  LED led_2 (.in(resultado[7]));
  LED led_3 (.in(resultado[5]));
  LED led_4 (.in(resultado[4]));
  LED led_5 (.in(resultado[3]));
  LED led_6 (.in(resultado[1]));
  LED led_7 (.in(resultado[2]));
  LED led_8 (.in(resultado[0]));

  // Other names for the same wires on the sheet: operando_1[7:0] = in_1; operando_2[7:0] = in_2
endmodule
